# Fritzing sketch pcg (saved by Fritzing 0.9.2b)
breadboards: 4

parts:
  Raspberry_Pi_A1 = Raspberry Pi A
  DI1 = 7-Segment LED Display [package=THT]
  DI2 = 7-Segment LED Display [package=THT]
  U1 = 74HC595 SMD [package="SO16 [SMD]"]
  U2 = 74HC595 SMD [package="SO16 [SMD]"]
  S1 = Pushbutton [package=THT]
  S2 = Pushbutton [package=THT]
  S3 = Pushbutton [package=THT]
  S4 = Pushbutton [package=THT]
  S5 = Pushbutton [package=THT]
  S6 = Pushbutton [package=THT]
  S7 = Pushbutton [package=THT]
  S9 = Pushbutton [package=THT]
  S10 = Pushbutton [package=THT]
  J1 = Piezo Speaker
  Q1 = PNP-Transistor [package="TO92 [THT]"]
  R1 = Resistor [tolerance=±5% resistance=1k package=THT]
  LED1 = smd LED [color="Green (555nm)" package="0805 [SMD]"]
  LED3 = smd LED [color="Red (633nm)" package="0805 [SMD]"]
  LED7 = smd LED [color="Green (565nm)" package="0805 [SMD]"]
  LED9 = smd LED [color="Green (555nm)" package="0805 [SMD]"]
  LED10 = smd LED [color="Green (555nm)" package="0805 [SMD]"]
  LED11 = smd LED [color="Green (555nm)" package="0805 [SMD]"]
  LED12 = smd LED [color="Green (555nm)" package="0805 [SMD]"]
  LED13 = smd LED [color="Green (555nm)" package="0805 [SMD]"]
  LED14 = smd LED [color="Green (555nm)" package="0805 [SMD]"]
  LED15 = smd LED [color="Green (555nm)" package="0805 [SMD]"]
  LED16 = smd LED [color="Green (555nm)" package="0805 [SMD]"]
  LED17 = smd LED [color="Red (633nm)" package="0805 [SMD]"]
  R2 = Resistor [tolerance=±5% resistance=1k package=THT]
  R3 = Resistor [tolerance=±5% resistance=1k package=THT]

nets:
  VCC: Raspberry_Pi_A1.5V, U1.MR, U1.VCC, U2.MR, U2.VCC, J1.pin2
  N1: Raspberry_Pi_A1.GPIO_2, R1.Pin_1
  N2: Raspberry_Pi_A1.GPIO_3, S3.leg1
  GND: Raspberry_Pi_A1.GND, U1.GND, U2.GND, S1.leg0, S2.leg0, S3.leg0, S4.leg0, S5.leg0, S6.leg0, S7.leg0, S9.leg0, S10.leg0, Q1.C, R2.Pin_1, R3.Pin_1
  N3: Raspberry_Pi_A1.GPIO_23, LED1.cathode, LED11.cathode, LED13.anode, LED14.cathode, LED15.cathode, LED16.cathode
  N4: Raspberry_Pi_A1.GPIO_14, S10.leg1
  N5: Raspberry_Pi_A1.GPIO_15, S2.leg1
  N6: Raspberry_Pi_A1.GPIO_17, U1.ST_CP, U2.ST_CP
  N7: Raspberry_Pi_A1.GPIO_18, U1.DS
  N8: Raspberry_Pi_A1.GPIO_27, U1.SH_CP, U2.SH_CP
  N9: Raspberry_Pi_A1.GPIO_22, LED3.cathode, LED9.anode, LED12.anode, LED13.cathode, LED16.anode, LED17.anode
  N10: Raspberry_Pi_A1.GPIO_4, S4.leg1
  N11: Raspberry_Pi_A1.GPIO_24, LED1.anode, LED7.cathode, LED9.cathode, LED10.cathode, LED11.anode, LED12.cathode
  N12: Raspberry_Pi_A1.GPIO_10, S7.leg1
  N13: Raspberry_Pi_A1.GPIO_9, S6.leg1
  N14: Raspberry_Pi_A1.GPIO_11, S1.leg1
  N15: Raspberry_Pi_A1.GPIO_8, S9.leg1, LED3.anode, LED7.anode, LED10.anode, LED14.anode, LED15.anode, LED17.cathode
  N16: Raspberry_Pi_A1.GPIO_7, S5.leg1
  N17: DI1.commAnode#2, R2.Pin_0
  N18: DI2.cathodeE, U1.Q4
  N19: DI2.cathodeD, U1.Q3
  N20: DI2.commAnode#2, R3.Pin_0
  N21: DI2.cathodeC, U1.Q2
  N22: DI2.cathodeDP, U1.Q7
  N23: DI2.cathodeB, U1.Q1
  N24: DI2.cathodeA, U1.Q0
  N25: DI2.cathodeF, U1.Q5
  N26: DI2.cathodeG, U1.Q6
  N27: U1.Q7', U2.DS
  N28: J1.pin1, Q1.E
  N29: Q1.B, R1.Pin_0

notes:
  Left LED blue wires similar to right one
  CharliePlexing 12 LEDs
  9 Plates on front act like switches
